// Logisim project Project 4.circ as structural Verilog
module _8_bit_Registry (
  input  [7:0] D,
  input  C,
  input  Reset,
  input  Write,
  output [7:0] Q
);

  D_Flip_Flop d_ff_1 (.clk(C), .D(D[0]), .Q(Q[0]), .en(Write), .reset(Reset));  // open: Qn, preset
  D_Flip_Flop d_ff_2 (.clk(C), .D(D[1]), .Q(Q[1]), .en(Write), .reset(Reset));  // open: Qn, preset
  D_Flip_Flop d_ff_3 (.clk(C), .D(D[2]), .Q(Q[2]), .en(Write), .reset(Reset));  // open: Qn, preset
  D_Flip_Flop d_ff_4 (.clk(C), .D(D[3]), .Q(Q[3]), .en(Write), .reset(Reset));  // open: Qn, preset
  D_Flip_Flop d_ff_5 (.clk(C), .D(D[4]), .Q(Q[4]), .en(Write), .reset(Reset));  // open: Qn, preset
  D_Flip_Flop d_ff_6 (.clk(C), .D(D[5]), .Q(Q[5]), .en(Write), .reset(Reset));  // open: Qn, preset
  D_Flip_Flop d_ff_7 (.clk(C), .D(D[6]), .Q(Q[6]), .en(Write), .reset(Reset));  // open: Qn, preset
  D_Flip_Flop d_ff_8 (.clk(C), .D(D[7]), .Q(Q[7]), .en(Write), .reset(Reset));  // open: Qn, preset
endmodule

module Counter (
  input  [7:0] D,
  input  C,
  output [7:0] out_3
);

  wire comparator_1_lt, not_1_out, not_2_out, real_8_bit_cla_1_out_4;
  wire [7:0] real_8_bit_cla_1_out_3;

  _8_bit_Registry u_8_bit_registry_1 (
    .D(real_8_bit_cla_1_out_3), .C(C), .Reset(not_1_out), .Write(not_2_out), .Q(out_3));
  real_8_bit_CLA real_8_bit_cla_1 (
    .in_1(out_3), .in_2(8'h1), .out_3(real_8_bit_cla_1_out_3), .out_4(real_8_bit_cla_1_out_4));
  Comparator comparator_1 (.a(out_3), .b(D), .lt(comparator_1_lt));  // open: gt, eq
  not not_1 (not_1_out, comparator_1_lt);
  not not_2 (not_2_out, real_8_bit_cla_1_out_4);
endmodule

module State_traffic_light (
  input  C
);

  wire comparator_1_eq, comparator_2_eq, decoder_1_out0, decoder_1_out1, decoder_1_out2, decoder_2_out0,
       decoder_2_out1, decoder_2_out2, decoder_2_out3, or_1_out;
  wire [1:0] bit_extender_1_out, bit_extender_2_out;
  wire [7:0] counter_1_out_3, counter_2_out_3, multiplexer_1_out, multiplexer_2_out, Time_Counter_2_out_3,
       Time_Counter_out_3;

  Multiplexer #(.select(2), .width(8)) multiplexer_1 (
    .in0(8'h10), .in1(8'h8), .in2(8'h20), .out(multiplexer_1_out), .sel(bit_extender_1_out));  // open: in3, en
  Counter Time_Counter (.D(multiplexer_1_out), .C(C), .out_3(Time_Counter_out_3));
  Multiplexer #(.select(2), .width(8)) multiplexer_2 (
    .in0(8'h1c), .in1(8'h10), .in2(8'h8), .in3(8'h2), .out(multiplexer_2_out), .sel(bit_extender_2_out));  // open: en
  Counter Time_Counter_2 (.D(multiplexer_2_out), .C(C), .out_3(Time_Counter_2_out_3));
  Comparator comparator_1 (.a(Time_Counter_out_3), .b({8{1'b0}}), .eq(comparator_1_eq));  // open: gt, lt
  Comparator comparator_2 (.a(Time_Counter_2_out_3), .b({8{1'b0}}), .eq(comparator_2_eq));  // open: gt, lt
  Bit_Extender #(.out_width(2)) bit_extender_1 (.in(counter_1_out_3), .out(bit_extender_1_out));
  Counter counter_1 (.D(8'h3), .C(comparator_1_eq), .out_3(counter_1_out_3));
  Bit_Extender #(.out_width(2)) bit_extender_2 (.in(counter_2_out_3), .out(bit_extender_2_out));
  Counter counter_2 (.D(8'h4), .C(comparator_2_eq), .out_3(counter_2_out_3));
  LED led_1 (.in(decoder_1_out2));
  Decoder #(.select(2)) decoder_1 (
    .out0(decoder_1_out0), .out1(decoder_1_out1), .out2(decoder_1_out2), .sel(bit_extender_1_out));  // open: out3, en
  LED led_2 (.in(decoder_1_out1));
  LED led_3 (.in(decoder_1_out0));
  Decoder #(.select(2)) decoder_2 (
    .out0(decoder_2_out0), .out1(decoder_2_out1), .out2(decoder_2_out2), .out3(decoder_2_out3),
    .sel(bit_extender_2_out));  // open: en
  or or_1 (or_1_out, decoder_2_out0, decoder_2_out3);
  LED led_4 (.in(or_1_out));
  LED led_5 (.in(decoder_2_out2));
  LED led_6 (.in(decoder_2_out1));

  // Notes on the sheet:
  //   Light 1
  //   Light 2
endmodule

module Register_file (
);

  _8_bit_Registry u_8_bit_registry_1 ();  // open: D, C, Reset, Write, Q
  _8_bit_Registry u_8_bit_registry_2 ();  // open: D, C, Reset, Write, Q
  _8_bit_Registry u_8_bit_registry_3 ();  // open: D, C, Reset, Write, Q
  _8_bit_Registry u_8_bit_registry_4 ();  // open: D, C, Reset, Write, Q
  _8_bit_Registry u_8_bit_registry_5 ();  // open: D, C, Reset, Write, Q
  _8_bit_Registry u_8_bit_registry_6 ();  // open: D, C, Reset, Write, Q
  _8_bit_Registry u_8_bit_registry_7 ();  // open: D, C, Reset, Write, Q
  _8_bit_Registry u_8_bit_registry_8 ();  // open: D, C, Reset, Write, Q
  _8_bit_Registry u_8_bit_registry_9 ();  // open: D, C, Reset, Write, Q
  _8_bit_Registry u_8_bit_registry_10 ();  // open: D, C, Reset, Write, Q
  _8_bit_Registry u_8_bit_registry_11 ();  // open: D, C, Reset, Write, Q
  _8_bit_Registry u_8_bit_registry_12 ();  // open: D, C, Reset, Write, Q
  _8_bit_Registry u_8_bit_registry_13 ();  // open: D, C, Reset, Write, Q
  _8_bit_Registry u_8_bit_registry_14 ();  // open: D, C, Reset, Write, Q
  _8_bit_Registry u_8_bit_registry_15 ();  // open: D, C, Reset, Write, Q
  _8_bit_Registry u_8_bit_registry_16 ();  // open: D, C, Reset, Write, Q
endmodule
