// Logisim project SD_Group50.circ as structural Verilog: 6 circuits, main circuit main
module main (
  input  [15:0] Instruction,
  input  Clock,
  input  Reset,
  input  [7:0] D_read,
  output [7:0] pc,
  output [7:0] r0,
  output [7:0] r1,
  output [7:0] r2,
  output [7:0] r3,
  output [7:0] r4,
  output [7:0] r5,
  output [7:0] r6,
  output [7:0] r7,
  output [7:0] r8,
  output [7:0] r9,
  output [7:0] r10,
  output [7:0] r11,
  output [7:0] r12,
  output [7:0] r13,
  output [7:0] r14,
  output [7:0] r15,
  output halt,
  output [7:0] A,
  output [7:0] D,
  output str,
  output C,
  output ld,
  output clr,
  output [7:0] out_29,
  output Overflow,
  output [7:0] out_31,
  output [7:0] out_32,
  output [7:0] out_33,
  output [7:0] out_34,
  output [7:0] out_35,
  output [7:0] out_36,
  output [7:0] out_37,
  output [7:0] out_38,
  output [7:0] out_39,
  output [7:0] out_40,
  output [7:0] out_41,
  output [7:0] out_42,
  output [7:0] out_43,
  output [7:0] out_44,
  output [7:0] out_45
);

  wire clock_1_out, comparator_3_eq, imm_out, not_1_out, or_1_out, undriven, undriven_2, undriven_3,
       undriven_4, write_out;
  wire [3:0] _0001_out, _1010_out, _1011_out, bit_extender_1_out, bit_extender_2_out, bit_extender_3_out,
       bit_extender_4_out, Else_out, multiplexer_1_out, or_2_out;
  wire [7:0] bit_extender_5_out, multiplexer_2_out, multiplexer_3_out, ram_2_data, Register_file_rs_content;
  wire [15:0] ram_1_data;

  Halt halt_1 (.instruction(ram_1_data), .clock(clock_1_out), .reset(clr), .halt(halt));
  Clock clock_1 (.out(clock_1_out));
  Button u_reset (.out(clr));
  and and_1 (C, ~halt, clock_1_out);  // AND_Gate
  _8_bit_PC u_8_bit_pc_1 (
    .Branch_relative(1'b0), .Branch_absolute(1'b0), .Branch_value({8{1'b0}}), .C(C), .Reset(clr),
    .Adress_in_instruction_memory(pc));
  RAM #(.dataWidth(16)) ram_1 (.addr(pc), .data(ram_1_data), .ld(1'b1), .clr(clr));  // open: sel, clk
  Register register_1 ();  // open: D, en, Q, clk, clr
  or write (write_out, not_1_out, comparator_3_eq, ld);
  Multiplexer #(.width(4)) multiplexer_1 (
    .in0(ram_1_data[3:0]), .in1(ram_1_data[11:8]), .out(multiplexer_1_out), .sel(imm_out));  // open: en
  Multiplexer #(.width(8)) multiplexer_2 (.in0(A), .in1(D_read), .out(multiplexer_2_out), .sel(ld));  // open: en
  not not_1 (not_1_out, or_1_out);
  or or_1 (or_1_out, comparator_3_eq, ld, str);
  Comparator #(.width(4)) comparator_1 (.a(4'b1011), .b(ram_1_data[15:12]), .eq(str));  // open: gt, lt
  Comparator #(.width(4)) comparator_2 (.a(4'b1010), .b(ram_1_data[15:12]), .eq(ld));  // open: gt, lt
  Comparator #(.width(4)) comparator_3 (.a(4'b0001), .b(ram_1_data[15:12]), .eq(comparator_3_eq));  // open: gt, lt
  assign bit_extender_1_out = {{3{not_1_out}}, not_1_out};  // Bit_Extender bit_extender_1
  assign bit_extender_2_out = {{3{str}}, str};  // Bit_Extender bit_extender_2
  assign bit_extender_3_out = {{3{ld}}, ld};  // Bit_Extender bit_extender_3
  assign bit_extender_4_out = {{3{comparator_3_eq}}, comparator_3_eq};  // Bit_Extender bit_extender_4
  assign Else_out = ram_1_data[15:12] & bit_extender_1_out;  // AND_Gate Else, 4 bits wide
  assign _1011_out = bit_extender_2_out & 4'b0100;  // AND_Gate _1011, 4 bits wide
  assign _1010_out = bit_extender_3_out & 4'b0100;  // AND_Gate _1010, 4 bits wide
  assign _0001_out = bit_extender_4_out & ram_1_data[3:0];  // AND_Gate _0001, 4 bits wide
  assign or_2_out = _0001_out | _1010_out | _1011_out | Else_out;  // OR_Gate or_2, 4 bits wide
  Register_File_2_0 Register_file (
    .rs_in(ram_1_data[7:4]), .rt_in(multiplexer_1_out), .\input (multiplexer_2_out), .in_4(ram_1_data[11:8]),
    .clock(C), .reset(clr), .write(write_out), .out_10(out_29), .out_11(out_31), .out_12(out_32),
    .out_13(out_33), .out_14(out_34), .out_15(out_35), .out_16(out_36), .out_17(out_37), .out_18(out_38),
    .out_19(out_39), .out_20(out_40), .out_21(out_41), .out_22(out_42), .out_23(out_43), .out_24(out_44),
    .out_25(out_45), .rs_content(Register_file_rs_content), .rt_content(D));
  assign bit_extender_5_out = {{4{1'b0}}, ram_1_data[3:0]};  // Bit_Extender bit_extender_5
  or imm (imm_out, ld, str);
  Multiplexer #(.width(8)) multiplexer_3 (
    .in0(D), .in1(bit_extender_5_out), .out(multiplexer_3_out), .sel(imm_out));  // open: en
  _8_bit_ALU u_8_bit_alu_1 (
    .ALU_code(or_2_out), .a(Register_file_rs_content), .b(multiplexer_3_out), .result(A), .overflow(Overflow));
  RAM #(.bus("separate")) ram_2 (
    .data(ram_2_data), .str(undriven), .clk(undriven_2), .ld(undriven_3), .clr(undriven_4));  // open: addr, din, sel

  // Notes on the sheet:
  //   current instruction
  //   clock signal
  //   reset button
  //   op
  //   rd
  //   rs
  //   rt
  //   rs en rt
  //   Else -> use op as op code
  //   op add
  //   Opcode == 0001 -> use rt as op code
  //   Opcode == 1010 -> lb at position (rs+rt) to rd
  //   Opcode == 1011 -> sb at position rd to (rs+rt) 
  //   Resultaat vd ALU
  //   DO NOT CHANGE THE INPUTS AND OUTPUTS OF THIS CIRCUIT! Do not add/remove inputs or outputs. Do not even change their location or orientation.
  //   rt
  //   lb
  //   adress + offset
  //   rt
  //   gelezen lb
endmodule

module Halt (
  input  [15:0] instruction,
  input  clock,
  input  reset,
  output halt
);

  wire and_1_out, comparator_1_eq, comparator_2_gt, counter_1_carry, or_1_out, or_2_out;
  wire [11:0] counter_1_q;

  Comparator #(.width(16), .mode("unsigned")) comparator_1 (
    .a(instruction), .b({16{1'b0}}), .eq(comparator_1_eq));  // open: gt, lt
  Counter #(.width(12), .max('hfff), .trigger("falling")) counter_1 (
    .Q(counter_1_q), .carry(counter_1_carry), .clk(clock), .clr(reset));  // open: load, D, count
  or or_1 (or_1_out, comparator_1_eq, counter_1_carry);
  Comparator #(.width(12), .mode("unsigned")) comparator_2 (
    .a(counter_1_q), .b({12{1'b0}}), .gt(comparator_2_gt));  // open: eq, lt
  or or_2 (or_2_out, halt, and_1_out);
  and and_1 (and_1_out, or_1_out, comparator_2_gt);
  Register #(.width(1)) register_1 (.D(or_2_out), .Q(halt), .clk(clock), .clr(reset));  // open: en

  // Notes on the sheet:
  //   halt becomes and stays asserted if the instruction is 0000 (not in the first clock cycle) or the end of the counter is reached (2^12)
endmodule

module _8_bit_PC (
  input  Branch_relative,
  input  Branch_absolute,
  input  [7:0] Branch_value,
  input  C,
  input  Reset,
  output [7:0] Adress_in_instruction_memory
);

  wire and_1_out, and_2_out, and_3_out, not_1_out, not_2_out, not_3_out, not_4_out;
  wire [7:0] adder_1_out, adder_2_out, and_4_out, and_5_out, and_6_out, bit_extender_1_out,
       bit_extender_2_out, bit_extender_3_out, or_1_out;

  Adder adder_1 (.a(Adress_in_instruction_memory), .b(8'h1), .out(adder_1_out));  // open: cin, cout
  Adder adder_2 (.a(Adress_in_instruction_memory), .b(Branch_value), .out(adder_2_out));  // open: cin, cout
  not not_1 (not_1_out, Branch_relative);
  not not_2 (not_2_out, Branch_absolute);
  not not_3 (not_3_out, Branch_absolute);
  not not_4 (not_4_out, Branch_relative);
  and and_1 (and_1_out, not_1_out, not_2_out);
  and and_2 (and_2_out, Branch_relative, not_3_out);
  and and_3 (and_3_out, not_4_out, Branch_absolute);
  assign bit_extender_1_out = {{7{and_1_out}}, and_1_out};  // Bit_Extender bit_extender_1
  assign bit_extender_2_out = {{7{and_2_out}}, and_2_out};  // Bit_Extender bit_extender_2
  assign bit_extender_3_out = {{7{and_3_out}}, and_3_out};  // Bit_Extender bit_extender_3
  assign and_4_out = bit_extender_1_out & adder_1_out;  // AND_Gate and_4, 8 bits wide
  assign and_5_out = bit_extender_2_out & adder_2_out;  // AND_Gate and_5, 8 bits wide
  assign and_6_out = bit_extender_3_out & Branch_value;  // AND_Gate and_6, 8 bits wide
  assign or_1_out = and_6_out | and_5_out | and_4_out;  // OR_Gate or_1, 8 bits wide
  _8_bit_Registry Register__containing_current_adress (
    .D(or_1_out), .C(C), .Reset(Reset), .Write(C), .Q(Adress_in_instruction_memory));

  // Notes on the sheet:
  //   CALCULATING THE NEXT ADRESS
  //   Default: +1 each cycle
  //   Branch relative: +Branch value
  //   Branch absolute: = Branch value
  //   Instruction can only change once per clock cycle, so only write once per clock cycle
  //   DECIDING THE NEXT ADRESS
  //   Default: Not relative, not absolute
  //   Branch relative: Relative, not absolute
  //   Branch absolute: Not relative, absolute
endmodule

module Datapath (
  input  [15:0] Instruction,
  input  Clock,
  input  Reset,
  input  [7:0] D_read,
  output [7:0] A,
  output [7:0] D,
  output str,
  output C,
  output ld,
  output clr,
  output [7:0] out_11,
  output Overflow,
  output [7:0] out_13,
  output [7:0] out_14,
  output [7:0] out_15,
  output [7:0] out_16,
  output [7:0] out_17,
  output [7:0] out_18,
  output [7:0] out_19,
  output [7:0] out_20,
  output [7:0] out_21,
  output [7:0] out_22,
  output [7:0] out_23,
  output [7:0] out_24,
  output [7:0] out_25,
  output [7:0] out_26,
  output [7:0] out_27
);

  wire comparator_3_eq, imm_out, not_1_out, or_1_out, write_out;
  wire [3:0] _0001_out, _1010_out, _1011_out, bit_extender_1_out, bit_extender_2_out, bit_extender_3_out,
       bit_extender_4_out, Else_out, multiplexer_1_out, or_2_out;
  wire [7:0] bit_extender_5_out, multiplexer_2_out, multiplexer_3_out, Register_file_rs_content;

  or write (write_out, not_1_out, comparator_3_eq, ld);
  Multiplexer #(.width(4)) multiplexer_1 (
    .in0(Instruction[3:0]), .in1(Instruction[11:8]), .out(multiplexer_1_out), .sel(imm_out));  // open: en
  Multiplexer #(.width(8)) multiplexer_2 (.in0(A), .in1(D_read), .out(multiplexer_2_out), .sel(ld));  // open: en
  not not_1 (not_1_out, or_1_out);
  or or_1 (or_1_out, comparator_3_eq, ld, str);
  Comparator #(.width(4)) comparator_1 (.a(4'b1011), .b(Instruction[15:12]), .eq(str));  // open: gt, lt
  Comparator #(.width(4)) comparator_2 (.a(4'b1010), .b(Instruction[15:12]), .eq(ld));  // open: gt, lt
  Comparator #(.width(4)) comparator_3 (.a(4'b0001), .b(Instruction[15:12]), .eq(comparator_3_eq));  // open: gt, lt
  assign bit_extender_1_out = {{3{not_1_out}}, not_1_out};  // Bit_Extender bit_extender_1
  assign bit_extender_2_out = {{3{str}}, str};  // Bit_Extender bit_extender_2
  assign bit_extender_3_out = {{3{ld}}, ld};  // Bit_Extender bit_extender_3
  assign bit_extender_4_out = {{3{comparator_3_eq}}, comparator_3_eq};  // Bit_Extender bit_extender_4
  assign Else_out = Instruction[15:12] & bit_extender_1_out;  // AND_Gate Else, 4 bits wide
  assign _1011_out = bit_extender_2_out & 4'b0100;  // AND_Gate _1011, 4 bits wide
  assign _1010_out = bit_extender_3_out & 4'b0100;  // AND_Gate _1010, 4 bits wide
  assign _0001_out = bit_extender_4_out & Instruction[3:0];  // AND_Gate _0001, 4 bits wide
  assign or_2_out = _0001_out | _1010_out | _1011_out | Else_out;  // OR_Gate or_2, 4 bits wide
  Register_File_2_0 Register_file (
    .rs_in(Instruction[7:4]), .rt_in(multiplexer_1_out), .\input (multiplexer_2_out),
    .in_4(Instruction[11:8]), .clock(Clock), .reset(Reset), .write(write_out), .out_10(out_11),
    .out_11(out_13), .out_12(out_14), .out_13(out_15), .out_14(out_16), .out_15(out_17), .out_16(out_18),
    .out_17(out_19), .out_18(out_20), .out_19(out_21), .out_20(out_22), .out_21(out_23), .out_22(out_24),
    .out_23(out_25), .out_24(out_26), .out_25(out_27), .rs_content(Register_file_rs_content), .rt_content(D));
  assign bit_extender_5_out = {{4{1'b0}}, Instruction[3:0]};  // Bit_Extender bit_extender_5
  or imm (imm_out, ld, str);
  Multiplexer #(.width(8)) multiplexer_3 (
    .in0(D), .in1(bit_extender_5_out), .out(multiplexer_3_out), .sel(imm_out));  // open: en
  _8_bit_ALU u_8_bit_alu_1 (
    .ALU_code(or_2_out), .a(Register_file_rs_content), .b(multiplexer_3_out), .result(A), .overflow(Overflow));

  assign C = Clock;
  assign clr = Reset;

  // Notes on the sheet:
  //   op
  //   rs
  //   rd
  //   rt
  //   rs en rt
  //   Else -> use op as op code
  //   op add
  //   Opcode == 0001 -> use rt as op code
  //   Opcode == 1010 -> lb at position (rs+rt) to rd
  //   Opcode == 1011 -> sb at position rd to (rs+rt) 
  //   rt
  //   Resultaat vd ALU
  //   lb
  //   adress + offset
  //   rt
  //   gelezen lb
endmodule

module equal (
  input  [3:0] in_1,
  input  [3:0] in_2,
  output out_3
);

  wire and_1_out, and_2_out, and_3_out, and_4_out, not_1_out, not_2_out, not_3_out, not_4_out, or_1_out,
       or_2_out, or_3_out, or_4_out, or_5_out, or_6_out, or_7_out, or_8_out;

  or or_1 (or_1_out, in_1[0], in_2[0]);
  and and_1 (and_1_out, in_1[0], in_2[0]);
  or or_2 (or_2_out, in_1[1], in_2[1]);
  and and_2 (and_2_out, in_1[1], in_2[1]);
  or or_3 (or_3_out, in_1[2], in_2[2]);
  and and_3 (and_3_out, in_1[2], in_2[2]);
  or or_4 (or_4_out, in_2[3], in_1[3]);
  and and_4 (and_4_out, in_2[3], in_1[3]);
  not not_1 (not_1_out, or_1_out);
  or or_5 (or_5_out, not_1_out, and_1_out);
  not not_2 (not_2_out, or_2_out);
  or or_6 (or_6_out, not_2_out, and_2_out);
  not not_3 (not_3_out, or_3_out);
  or or_7 (or_7_out, not_3_out, and_3_out);
  not not_4 (not_4_out, or_4_out);
  or or_8 (or_8_out, not_4_out, and_4_out);
  and and_5 (out_3, or_5_out, or_6_out, or_7_out, or_8_out);
endmodule

module sign_add (
  input  [3:0] in_1,
  input  [7:0] in_2,
  output [7:0] out_3
);

  wire and_1_out, not_1_out, not_2_out, or_1_out, or_2_out;
  wire [7:0] adder_1_out, bit_extender_1_out, subtractor_1_out;

  assign bit_extender_1_out = {{4{in_1[3]}}, in_1};  // Bit_Extender bit_extender_1
  or or_1 (or_1_out, in_1[3], in_2[7]);
  not not_1 (not_1_out, or_1_out);
  or or_2 (or_2_out, not_1_out, and_1_out);
  and and_1 (and_1_out, in_1[3], in_2[7]);
  Adder adder_1 (.a(bit_extender_1_out), .b(in_2), .out(adder_1_out));  // open: cin, cout
  Subtractor subtractor_1 (.a(bit_extender_1_out), .b(in_2), .out(subtractor_1_out));  // open: bin, bout
  not not_2 (not_2_out, or_2_out);
  Multiplexer #(.width(8)) multiplexer_1 (
    .in0(adder_1_out), .in1(subtractor_1_out), .out(out_3), .sel(not_2_out));  // open: en

  // Notes on the sheet:
  //   doet add wanneer bij beide getallen de eerst dezelfde waarde heeft
  //   een neg met neg optellen geeft meer neg
  //   pos optellen met neg trekt het pos getal af van het neg
  //   neg optellen met pos trekt het neg getal af van het pos , heeft zelfde effect als hierboven
  //   checkt of eerste getal zxelfde is 
endmodule
